// Logisim project adder_test.circ as structural Verilog: 2 circuits, main circuit main
module main (
  input  sub,
  input  [15:0] A,
  input  [15:0] B,
  output [15:0] result,
  output ovf
);

  wire n1_bit_fa_1_cout, n1_bit_fa_2_cout, n1_bit_fa_3_cout, n1_bit_fa_4_cout, n1_bit_fa_5_cout,
       n1_bit_fa_6_cout, n1_bit_fa_7_cout, n1_bit_fa_8_cout, n1_bit_fa_9_cout, n1_bit_fa_10_cout,
       n1_bit_fa_11_cout, n1_bit_fa_12_cout, n1_bit_fa_13_cout, n1_bit_fa_14_cout, n1_bit_fa_15_cout,
       n1_bit_fa_16_cout, xor_1_out, xor_2_out, xor_3_out, xor_4_out, xor_5_out, xor_6_out, xor_7_out,
       xor_8_out, xor_9_out, xor_10_out, xor_11_out, xor_12_out, xor_13_out, xor_14_out, xor_15_out,
       xor_16_out;

  xor xor_1 (xor_1_out, sub, B[0]);
  xor xor_2 (xor_2_out, sub, B[1]);
  xor xor_3 (xor_3_out, sub, B[2]);
  xor xor_4 (xor_4_out, sub, B[3]);
  xor xor_5 (xor_5_out, sub, B[4]);
  xor xor_6 (xor_6_out, sub, B[5]);
  xor xor_7 (xor_7_out, sub, B[6]);
  xor xor_8 (xor_8_out, sub, B[7]);
  xor xor_9 (xor_9_out, sub, B[8]);
  xor xor_10 (xor_10_out, sub, B[9]);
  xor xor_11 (xor_11_out, sub, B[10]);
  xor xor_12 (xor_12_out, sub, B[11]);
  xor xor_13 (xor_13_out, sub, B[12]);
  xor xor_14 (xor_14_out, sub, B[14]);
  xor xor_15 (xor_15_out, sub, B[14]);
  xor xor_16 (xor_16_out, sub, B[15]);
  _1_bit_FA u_1_bit_fa_1 (.A(A[0]), .B(xor_1_out), .Cin(sub), .Cout(n1_bit_fa_1_cout), .Sum(result[0]));
  _1_bit_FA u_1_bit_fa_2 (.A(A[1]), .B(xor_2_out), .Cin(n1_bit_fa_1_cout), .Cout(n1_bit_fa_2_cout), .Sum(result[1]));
  _1_bit_FA u_1_bit_fa_3 (.A(A[2]), .B(xor_3_out), .Cin(n1_bit_fa_2_cout), .Cout(n1_bit_fa_3_cout), .Sum(result[2]));
  _1_bit_FA u_1_bit_fa_4 (.A(A[3]), .B(xor_4_out), .Cin(n1_bit_fa_3_cout), .Cout(n1_bit_fa_4_cout), .Sum(result[3]));
  _1_bit_FA u_1_bit_fa_5 (.A(A[4]), .B(xor_5_out), .Cin(n1_bit_fa_4_cout), .Cout(n1_bit_fa_5_cout), .Sum(result[4]));
  _1_bit_FA u_1_bit_fa_6 (.A(A[5]), .B(xor_6_out), .Cin(n1_bit_fa_5_cout), .Cout(n1_bit_fa_6_cout), .Sum(result[5]));
  _1_bit_FA u_1_bit_fa_7 (.A(A[6]), .B(xor_7_out), .Cin(n1_bit_fa_6_cout), .Cout(n1_bit_fa_7_cout), .Sum(result[6]));
  _1_bit_FA u_1_bit_fa_8 (.A(A[7]), .B(xor_8_out), .Cin(n1_bit_fa_7_cout), .Cout(n1_bit_fa_8_cout), .Sum(result[7]));
  _1_bit_FA u_1_bit_fa_9 (.A(A[8]), .B(xor_9_out), .Cin(n1_bit_fa_8_cout), .Cout(n1_bit_fa_9_cout), .Sum(result[8]));
  _1_bit_FA u_1_bit_fa_10 (.A(A[9]), .B(xor_10_out), .Cin(n1_bit_fa_9_cout), .Cout(n1_bit_fa_10_cout), .Sum(result[9]));
  _1_bit_FA u_1_bit_fa_11 (
    .A(A[10]), .B(xor_11_out), .Cin(n1_bit_fa_10_cout), .Cout(n1_bit_fa_11_cout), .Sum(result[10]));
  _1_bit_FA u_1_bit_fa_12 (
    .A(A[11]), .B(xor_12_out), .Cin(n1_bit_fa_11_cout), .Cout(n1_bit_fa_12_cout), .Sum(result[11]));
  _1_bit_FA u_1_bit_fa_13 (
    .A(A[12]), .B(xor_13_out), .Cin(n1_bit_fa_12_cout), .Cout(n1_bit_fa_13_cout), .Sum(result[12]));
  _1_bit_FA u_1_bit_fa_14 (
    .A(A[13]), .B(xor_14_out), .Cin(n1_bit_fa_13_cout), .Cout(n1_bit_fa_14_cout), .Sum(result[13]));
  _1_bit_FA u_1_bit_fa_15 (
    .A(A[14]), .B(xor_15_out), .Cin(n1_bit_fa_14_cout), .Cout(n1_bit_fa_15_cout), .Sum(result[14]));
  _1_bit_FA u_1_bit_fa_16 (
    .A(A[15]), .B(xor_16_out), .Cin(n1_bit_fa_15_cout), .Cout(n1_bit_fa_16_cout), .Sum(result[15]));
  xor xor_17 (ovf, n1_bit_fa_15_cout, n1_bit_fa_16_cout);

  assign B[13] = B[14];
endmodule

module _1_bit_FA (
  input  Cin,
  input  A,
  input  B,
  output Sum,
  output Cout
);

  wire and_1_out, and_2_out, xor_1_out;

  and and_1 (and_1_out, B, A);
  xor xor_1 (xor_1_out, A, B);
  or or_1 (Cout, and_1_out, and_2_out);
  and and_2 (and_2_out, xor_1_out, Cin);
  xor xor_2 (Sum, Cin, xor_1_out);
endmodule
