// Logisim project alu.circ as structural Verilog
module alu (
  input  [31:0] A,
  input  [31:0] B,
  input  [3:0] ALUSel,
  output [31:0] Result
);

  wire undriven;
  wire [31:0] addertest_1_sumout, and32_1_andout, comp32_1_negout, lshifter_1_wordout, main_1_result,
       main_2_result_high, or32_1_orout, rshifter_1_shiftout, shiftrarith_1_outp, slt4bit_1_sltout,
       sub32_1_subout, xor32_1_xorout;

  and32 and32_1 (.a1(A), .b1(B), .andout(and32_1_andout));
  or32 or32_1 (.ain(A), .bin(B), .orout(or32_1_orout));
  xor32 xor32_1 (.ain(A), .bin(B), .xorout(xor32_1_xorout));
  comp32 comp32_1 (.a1(A), .negout(comp32_1_negout));
  addertest addertest_1 (.carryin(undriven), .ain(A), .bin(B), .sumout(addertest_1_sumout));  // open: co
  shiftrarith shiftrarith_1 (.arithin(A), .bin(B), .outp(shiftrarith_1_outp));
  lshifter lshifter_1 (.ainput(A), .bshift(B), .wordout(lshifter_1_wordout));
  rshifter rshifter_1 (.ain(A), .bshi(B), .shiftout(rshifter_1_shiftout));
  slt4bit slt4bit_1 (.ain(A), .bin(B), .sltout(slt4bit_1_sltout));
  sub32 sub32_1 (.ain(A), .bin(B), .subout(sub32_1_subout));  // open: carin, cout
  signedmultiplier_main main_1 (.A(A), .B(B), .result(main_1_result));  // open: result_high
  signedmultiplier_main main_2 (.A(A), .B(B), .result_high(main_2_result_high));  // open: result
  Multiplexer #(.select(4), .width(32), .enable("false")) multiplexer_1 (
    .in0(addertest_1_sumout), .in1(and32_1_andout), .in2(or32_1_orout), .in3(xor32_1_xorout),
    .in4(comp32_1_negout), .in5(shiftrarith_1_outp), .in6(lshifter_1_wordout), .in7(rshifter_1_shiftout),
    .in8(slt4bit_1_sltout), .in9(sub32_1_subout), .in10(main_1_result), .in11(main_2_result_high),
    .out(Result), .sel(ALUSel));  // open: in12, in13, in14, in15

  // Notes on the sheet:
  //   INPUTS to your circuit
  //   DON'T CHANGE THE LOCATIONS OF THE INPUTS AND OUTPUTS!
  //   OUTPUT from your circuit
endmodule

module helper_adder (
  input  carryin,
  input  [3:0] ain,
  input  [3:0] bin,
  output [3:0] sum,
  output carryout
);

  wire and_1_out, and_2_out, and_3_out, and_4_out, and_5_out, and_6_out, and_7_out, and_8_out, or_1_out,
       or_2_out, or_3_out, xor_1_out, xor_2_out, xor_5_out, xor_7_out;

  xor xor_1 (xor_1_out, ain[0], bin[0]);
  and and_1 (and_1_out, ain[0], bin[0]);
  xor xor_2 (xor_2_out, ain[1], bin[1]);
  and and_2 (and_2_out, ain[1], bin[1]);
  xor xor_3 (sum[0], carryin, xor_1_out);
  and and_3 (and_3_out, carryin, xor_1_out);
  or or_1 (or_1_out, and_3_out, and_1_out);
  xor xor_4 (sum[1], or_1_out, xor_2_out);
  and and_4 (and_4_out, xor_2_out, or_1_out);
  xor xor_5 (xor_5_out, ain[2], bin[2]);
  or or_2 (or_2_out, and_2_out, and_4_out);
  xor xor_6 (sum[2], or_2_out, xor_5_out);
  and and_5 (and_5_out, ain[2], bin[2]);
  and and_6 (and_6_out, xor_5_out, or_2_out);
  or or_3 (or_3_out, and_5_out, and_6_out);
  xor xor_7 (xor_7_out, ain[3], bin[3]);
  and and_7 (and_7_out, ain[3], bin[3]);
  xor xor_8 (sum[3], or_3_out, xor_7_out);
  and and_8 (and_8_out, xor_7_out, or_3_out);
  or or_4 (carryout, and_7_out, and_8_out);
endmodule

module adder32 (
  input  init,
  input  [31:0] ain,
  input  [31:0] bin,
  output overflow,
  output [31:0] sout
);

  wire helper_adder_1_carryout, helper_adder_2_carryout, helper_adder_3_carryout, helper_adder_5_carryout,
       helper_adder_6_carryout, helper_adder_7_carryout, helper_adder_8_carryout;
  wire [3:0] xor_1_out, xor_2_out, xor_3_out, xor_4_out, xor_5_out, xor_6_out, xor_7_out, xor_8_out;

  assign xor_1_out = bin[3:0] ^ {4{init}};  // XOR_Gate xor_1, 4 bits wide
  helper_adder helper_adder_1 (
    .carryin(init), .ain(ain[3:0]), .bin(xor_1_out), .sum(sout[3:0]), .carryout(helper_adder_1_carryout));
  assign xor_2_out = bin[11:8] ^ {4{init}};  // XOR_Gate xor_2, 4 bits wide
  assign xor_3_out = bin[7:4] ^ {4{init}};  // XOR_Gate xor_3, 4 bits wide
  assign xor_4_out = bin[31:28] ^ {4{init}};  // XOR_Gate xor_4, 4 bits wide
  helper_adder helper_adder_2 (
    .carryin(helper_adder_1_carryout), .ain(ain[7:4]), .bin(xor_3_out), .sum(sout[7:4]),
    .carryout(helper_adder_2_carryout));
  helper_adder helper_adder_3 (
    .carryin(helper_adder_2_carryout), .ain(ain[11:8]), .bin(xor_2_out), .sum(sout[11:8]),
    .carryout(helper_adder_3_carryout));
  assign xor_5_out = bin[15:12] ^ {4{init}};  // XOR_Gate xor_5, 4 bits wide
  helper_adder helper_adder_4 (
    .carryin(helper_adder_6_carryout), .ain(ain[31:28]), .bin(xor_4_out), .sum(sout[31:28]),
    .carryout(overflow));
  assign xor_6_out = bin[27:24] ^ {4{init}};  // XOR_Gate xor_6, 4 bits wide
  assign xor_7_out = bin[19:16] ^ {4{init}};  // XOR_Gate xor_7, 4 bits wide
  helper_adder helper_adder_5 (
    .carryin(helper_adder_3_carryout), .ain(ain[15:12]), .bin(xor_5_out), .sum(sout[15:12]),
    .carryout(helper_adder_5_carryout));
  assign xor_8_out = bin[23:20] ^ {4{init}};  // XOR_Gate xor_8, 4 bits wide
  helper_adder helper_adder_6 (
    .carryin(helper_adder_8_carryout), .ain(ain[27:24]), .bin(xor_6_out), .sum(sout[27:24]),
    .carryout(helper_adder_6_carryout));
  helper_adder helper_adder_7 (
    .carryin(helper_adder_5_carryout), .ain(ain[19:16]), .bin(xor_7_out), .sum(sout[19:16]),
    .carryout(helper_adder_7_carryout));
  helper_adder helper_adder_8 (
    .carryin(helper_adder_7_carryout), .ain(ain[23:20]), .bin(xor_8_out), .sum(sout[23:20]),
    .carryout(helper_adder_8_carryout));

  // Other names for the same wires on the sheet: a1[3:0] = ain[3:0]; a2[3:0] = ain[7:4]; a3[3:0] = ain[11:8];
  //   a4[3:0] = ain[15:12]; a5[3:0] = ain[19:16]; a6[3:0] = ain[23:20]; a7[3:0] = ain[27:24]; a8[3:0] = ain[31:28];
  //   b1[3:0] = bin[3:0]; b2[3:0] = bin[7:4]; b3[3:0] = bin[11:8]; b4[3:0] = bin[15:12]; b5[3:0] = bin[19:16];
  //   b6[3:0] = bin[23:20]; b7[3:0] = bin[27:24]; b8[3:0] = bin[31:28]; s1[3:0] = sout[3:0]; s2[3:0] = sout[7:4];
  //   s3[3:0] = sout[11:8]; s4[3:0] = sout[15:12]; s5[3:0] = sout[19:16]; s6[3:0] = sout[23:20];
  //   s7[3:0] = sout[27:24]; s8[3:0] = sout[31:28]; tc[3:0] = {4{init}}
endmodule

module lshifter (
  input  [31:0] ainput,
  input  [31:0] bshift,
  output [31:0] wordout
);

  wire not_1_out, yn;
  wire [3:0] testbshifter1_1_nibout, testbshifter1_2_nibout, testbshifter1_3_nibout, testbshifter1_4_nibout,
       testbshifter1_6_nibout, testbshifter1_7_nibout, testbshifter1_8_nibout;
  wire [4:0] muxin;
  wire [19:16] testbshifter1_5_nibout;
  wire [30:0] sub32_1_subout;

  // Probe on {ainput[27:0], 4'b0000}
  sub32 sub32_1 (.ain(bshift), .bin(32'h20), .subout({yn, sub32_1_subout}));  // open: carin, cout
  assign muxin = yn ? bshift[4:0] : 5'bz;  // Controlled_Buffer controlled_buffer_1
  not not_1 (not_1_out, yn);
  assign wordout = not_1_out ? {32{1'b0}} : 32'bz;  // Controlled_Buffer controlled_buffer_2
  assign muxin = not_1_out ? {5{1'b0}} : 5'bz;  // Controlled_Buffer controlled_buffer_3
  testbshifter1 testbshifter1_1 (
    .shiftin(muxin), .ain({32{1'b0}}), .nibin(ainput[3:0]), .nibout(testbshifter1_1_nibout));
  testbshifter1 testbshifter1_2 (
    .shiftin(muxin), .ain({ainput[3:0], {28{1'b0}}}), .nibin(ainput[7:4]), .nibout(testbshifter1_2_nibout));
  testbshifter1 testbshifter1_3 (
    .shiftin(muxin), .ain({ainput[7:0], {24{1'b0}}}), .nibin(ainput[11:8]), .nibout(testbshifter1_3_nibout));
  testbshifter1 testbshifter1_4 (
    .shiftin(muxin), .ain({ainput[11:0], {20{1'b0}}}), .nibin(ainput[15:12]), .nibout(testbshifter1_4_nibout));
  assign wordout = yn ? {testbshifter1_8_nibout, testbshifter1_7_nibout, testbshifter1_6_nibout, testbshifter1_5_nibout, testbshifter1_4_nibout, testbshifter1_3_nibout, testbshifter1_2_nibout, testbshifter1_1_nibout} : 32'bz;  // Controlled_Buffer controlled_buffer_4
  testbshifter1 testbshifter1_5 (
    .shiftin(muxin), .ain({ainput[15:0], {16{1'b0}}}), .nibin(ainput[19:16]), .nibout(testbshifter1_5_nibout));
  testbshifter1 testbshifter1_6 (
    .shiftin(muxin), .ain({ainput[19:0], {12{1'b0}}}), .nibin(ainput[23:20]), .nibout(testbshifter1_6_nibout));
  testbshifter1 testbshifter1_7 (
    .shiftin(muxin), .ain({ainput[23:0], {8{1'b0}}}), .nibin(ainput[27:24]), .nibout(testbshifter1_7_nibout));
  testbshifter1 testbshifter1_8 (
    .shiftin(muxin), .ain({ainput[27:0], 4'b0000}), .nibin(ainput[31:28]), .nibout(testbshifter1_8_nibout));

  // Other names for the same wires on the sheet: afive[31:12] = ainput[19:0]; afour[31:16] = ainput[15:0];
  //   aseven[31:4] = ainput[27:0]; asix[31:8] = ainput[23:0]; athree[31:20] = ainput[11:0]; atwo[31:24] = ainput[7:0];
  //   one[3:0] = ainput[7:4]; testerin[31:0] = ainput; two[3:0] = ainput[11:8]; three[3:0] = ainput[15:12];
  //   four[3:0] = ainput[19:16]; aone[31:28] = ainput[3:0]; zero[3:0] = ainput[3:0]; six[3:0] = ainput[27:24];
  //   five[3:0] = ainput[23:20]; maybe[4:0] = bshift[4:0]; outt[31:0] = wordout; seven[3:0] = ainput[31:28]
endmodule

module and32 (
  input  [31:0] a1,
  input  [31:0] b1,
  output [31:0] andout
);

  assign andout = a1 & b1;  // AND_Gate and_1, 32 bits wide
endmodule

module or32 (
  input  [31:0] ain,
  input  [31:0] bin,
  output [31:0] orout
);

  assign orout = ain | bin;  // OR_Gate or_1, 32 bits wide
endmodule

module xor32 (
  input  [31:0] ain,
  input  [31:0] bin,
  output [31:0] xorout
);

  assign xorout = ain ^ bin;  // XOR_Gate xor_1, 32 bits wide
endmodule

module comp32 (
  input  [31:0] a1,
  output [31:0] negout
);

  assign negout = a1 ^ {32{1'b1}};  // XOR_Gate xor_1, 32 bits wide
endmodule

module bshifter1 (
  input  [4:0] shiftamount,
  input  [31:0] shiftin,
  input  [3:0] nibble,
  output [3:0] nibout
);

  // Probe on shiftin[31:4]
  bshift3 bshift3_1 (
    .shifter({nibble[0], nibble[1], nibble[2], nibble[3], shiftin[31:4]}), .muxcon(shiftamount),
    .bitout(nibout[3]));
  bshift3 bshift3_2 (
    .shifter({nibble[0], nibble[1], nibble[2], shiftin[31:3]}), .muxcon(shiftamount), .bitout(nibout[2]));
  bshift3 bshift3_3 (.shifter({nibble[0], nibble[1], shiftin[31:2]}), .muxcon(shiftamount), .bitout(nibout[1]));
  bshift3 bshift3_4 (.shifter({nibble[0], shiftin[31:1]}), .muxcon(shiftamount), .bitout(nibout[0]));

  // Other names for the same wires on the sheet: a1[31:0] = {nibble[0], shiftin[31:1]}; shifts[31:0] = shiftin;
  //   a2[31:0] = {nibble[0], nibble[1], shiftin[31:2]}; a3[31:0] = {nibble[0], nibble[1], nibble[2], shiftin[31:3]};
  //   a4[31:0] = {nibble[0], nibble[1], nibble[2], nibble[3], shiftin[31:4]}; muxa[4:0] = shiftamount
endmodule

module bshift3 (
  input  [31:0] shifter,
  input  [4:0] muxcon,
  output bitout
);

  Multiplexer #(.select(5), .enable("false")) multiplexer_1 (
    .in0(shifter[31]), .in1(shifter[30]), .in2(shifter[29]), .in3(shifter[28]), .in4(shifter[27]),
    .in5(shifter[26]), .in6(shifter[25]), .in7(shifter[24]), .in8(shifter[23]), .in9(shifter[22]),
    .in10(shifter[21]), .in11(shifter[20]), .in12(shifter[19]), .in13(shifter[18]), .in14(shifter[17]),
    .in15(shifter[16]), .in16(shifter[15]), .in17(shifter[14]), .in18(shifter[13]), .in19(shifter[12]),
    .in20(shifter[11]), .in21(shifter[10]), .in22(shifter[9]), .in23(shifter[8]), .in24(shifter[7]),
    .in25(shifter[6]), .in26(shifter[5]), .in27(shifter[4]), .in28(shifter[3]), .in29(shifter[2]),
    .in30(shifter[1]), .in31(shifter[0]), .out(bitout), .sel(muxcon));
endmodule

module rshifter (
  input  [31:0] ain,
  input  [31:0] bshi,
  output [31:0] shiftout
);

  wire not_1_out, sbit, yn;
  wire [3:0] bshifter1r_1_nibout, bshifter1r_2_nibout, bshifter1r_3_nibout, bshifter1r_4_nibout,
       bshifter1r_6_nibout, bshifter1r_7_nibout, bshifter1r_8_nibout, zeroz;
  wire [4:0] muxin;
  wire [7:0] zeroo;
  wire [11:0] zerotw;
  wire [15:0] zerothr;
  wire [19:0] zerof;
  wire [19:16] bshifter1r_5_nibout;
  wire [23:0] zerofi;
  wire [27:0] zerosi;
  wire [30:0] sub32_1_subout;
  wire [31:0] aseven;

  // Probe on {4'b0000, ain[31:4]}
  // Probe on bshi
  // Probe on 32'h20
  sub32 sub32_1 (.ain(bshi), .bin(32'h20), .subout({yn, sub32_1_subout}));  // open: carin, cout
  // Probe on {yn, sub32_1_subout}
  assign zeroo = {{7{sbit}}, sbit};  // Bit_Extender bit_extender_1
  assign zerotw = {{11{sbit}}, sbit};  // Bit_Extender bit_extender_2
  assign zerothr = {{15{sbit}}, sbit};  // Bit_Extender bit_extender_3
  assign zerof = {{19{sbit}}, sbit};  // Bit_Extender bit_extender_4
  assign zerofi = {{23{sbit}}, sbit};  // Bit_Extender bit_extender_5
  assign zerosi = {{27{sbit}}, sbit};  // Bit_Extender bit_extender_6
  assign aseven = {{31{sbit}}, sbit};  // Bit_Extender bit_extender_7
  assign zeroz = {{3{sbit}}, sbit};  // Bit_Extender bit_extender_8
  assign muxin = yn ? bshi[4:0] : 5'bz;  // Controlled_Buffer controlled_buffer_1
  not not_1 (not_1_out, yn);
  assign shiftout = not_1_out ? {32{1'b0}} : 32'bz;  // Controlled_Buffer controlled_buffer_2
  assign muxin = not_1_out ? {5{1'b0}} : 5'bz;  // Controlled_Buffer controlled_buffer_3
  bshifter1r bshifter1r_1 (
    .sel(muxin), .shiftin({4'b0000, ain[31:4]}), .nibble(ain[3:0]), .nibout(bshifter1r_1_nibout));
  bshifter1r bshifter1r_2 (
    .sel(muxin), .shiftin({{8{1'b0}}, ain[31:8]}), .nibble(ain[7:4]), .nibout(bshifter1r_2_nibout));
  bshifter1r bshifter1r_3 (
    .sel(muxin), .shiftin({{12{1'b0}}, ain[31:12]}), .nibble(ain[11:8]), .nibout(bshifter1r_3_nibout));
  bshifter1r bshifter1r_4 (
    .sel(muxin), .shiftin({{16{1'b0}}, ain[31:16]}), .nibble(ain[15:12]), .nibout(bshifter1r_4_nibout));
  assign shiftout = yn ? {bshifter1r_8_nibout, bshifter1r_7_nibout, bshifter1r_6_nibout, bshifter1r_5_nibout, bshifter1r_4_nibout, bshifter1r_3_nibout, bshifter1r_2_nibout, bshifter1r_1_nibout} : 32'bz;  // Controlled_Buffer controlled_buffer_4
  bshifter1r bshifter1r_5 (
    .sel(muxin), .shiftin({{20{1'b0}}, ain[31:20]}), .nibble(ain[19:16]), .nibout(bshifter1r_5_nibout));
  bshifter1r bshifter1r_6 (
    .sel(muxin), .shiftin({{24{1'b0}}, ain[31:24]}), .nibble(ain[23:20]), .nibout(bshifter1r_6_nibout));
  bshifter1r bshifter1r_7 (
    .sel(muxin), .shiftin({ain[3:0], {28{1'b0}}}), .nibble(ain[27:24]), .nibout(bshifter1r_7_nibout));
  bshifter1r bshifter1r_8 (.sel(muxin), .shiftin(aseven), .nibble(ain[31:28]), .nibout(bshifter1r_8_nibout));
  // also tied to GND on the sheet: {aseven[0], aseven[1], aseven[2], aseven[3], aseven[4], aseven[5], aseven[6], aseven[7], aseven[8], aseven[9], aseven[10], aseven[11], aseven[12], aseven[13], aseven[14], aseven[15], aseven[16], aseven[17], aseven[18], aseven[19], aseven[20], aseven[21], aseven[22], aseven[23], aseven[24], aseven[25], aseven[26], aseven[27], aseven[28], aseven[29], aseven[30], aseven[31]}

  // Other names for the same wires on the sheet: aone[23:0] = ain[31:8]; azero[27:0] = ain[31:4];
  //   testerin[31:0] = ain; two[3:0] = ain[11:8]; asix[31:28] = ain[3:0]; zero[3:0] = ain[3:0];
  //   atwo[19:0] = ain[31:12]; three[3:0] = ain[15:12]; athree[15:0] = ain[31:16]; four[3:0] = ain[19:16];
  //   afour[11:0] = ain[31:20]; five[3:0] = ain[23:20]; afive[7:0] = ain[31:24]; six[3:0] = ain[27:24];
  //   seven[3:0] = ain[31:28]; one[3:0] = ain[7:4]; maybe[4:0] = bshi[4:0]; outt[31:0] = shiftout
endmodule

module shiftrarith (
  input  [31:0] arithin,
  input  [31:0] bin,
  output [31:0] outp
);

  wire not_1_out, yn;
  wire [3:0] bshifter1r_1_nibout, bshifter1r_2_nibout, bshifter1r_3_nibout, bshifter1r_4_nibout,
       bshifter1r_6_nibout, bshifter1r_7_nibout, bshifter1r_8_nibout, zeroz;
  wire [4:0] muxin;
  wire [19:16] bshifter1r_5_nibout;
  wire [30:0] sub32_1_subout;
  wire [31:0] aseven;
  wire [31:4] asix;
  wire [31:8] afive;
  wire [31:12] afour;
  wire [31:16] athree;
  wire [31:20] atwo;
  wire [31:24] aone;
  wire [31:28] azero;

  // Probe on arithin
  // Probe on {azero, arithin[31:4]}
  sub32 sub32_1 (.ain(bin), .bin(32'h20), .subout({yn, sub32_1_subout}));  // open: carin, cout
  assign muxin = yn ? bin[4:0] : 5'bz;  // Controlled_Buffer controlled_buffer_1
  not not_1 (not_1_out, yn);
  assign outp = not_1_out ? aseven : 32'bz;  // Controlled_Buffer controlled_buffer_2
  assign muxin = not_1_out ? {5{1'b0}} : 5'bz;  // Controlled_Buffer controlled_buffer_3
  assign zeroz = {{3{arithin[31]}}, arithin[31]};  // Bit_Extender bit_extender_1
  assign aone = {{7{arithin[31]}}, arithin[31]};  // Bit_Extender bit_extender_2
  assign atwo = {{11{arithin[31]}}, arithin[31]};  // Bit_Extender bit_extender_3
  assign athree = {{15{arithin[31]}}, arithin[31]};  // Bit_Extender bit_extender_4
  assign afour = {{19{arithin[31]}}, arithin[31]};  // Bit_Extender bit_extender_5
  assign afive = {{23{arithin[31]}}, arithin[31]};  // Bit_Extender bit_extender_6
  assign asix = {{27{arithin[31]}}, arithin[31]};  // Bit_Extender bit_extender_7
  assign aseven = {{31{arithin[31]}}, arithin[31]};  // Bit_Extender bit_extender_8
  bshifter1r bshifter1r_1 (
    .sel(muxin), .shiftin({azero, arithin[31:4]}), .nibble(arithin[3:0]), .nibout(bshifter1r_1_nibout));
  bshifter1r bshifter1r_2 (
    .sel(muxin), .shiftin({aone, arithin[31:8]}), .nibble(arithin[7:4]), .nibout(bshifter1r_2_nibout));
  bshifter1r bshifter1r_3 (
    .sel(muxin), .shiftin({atwo, arithin[31:12]}), .nibble(arithin[11:8]), .nibout(bshifter1r_3_nibout));
  bshifter1r bshifter1r_4 (
    .sel(muxin), .shiftin({athree, arithin[31:16]}), .nibble(arithin[15:12]), .nibout(bshifter1r_4_nibout));
  assign outp = yn ? {bshifter1r_8_nibout, bshifter1r_7_nibout, bshifter1r_6_nibout, bshifter1r_5_nibout, bshifter1r_4_nibout, bshifter1r_3_nibout, bshifter1r_2_nibout, bshifter1r_1_nibout} : 32'bz;  // Controlled_Buffer controlled_buffer_4
  bshifter1r bshifter1r_5 (
    .sel(muxin), .shiftin({afour, arithin[31:20]}), .nibble(arithin[19:16]), .nibout(bshifter1r_5_nibout));
  bshifter1r bshifter1r_6 (
    .sel(muxin), .shiftin({afive, arithin[31:24]}), .nibble(arithin[23:20]), .nibout(bshifter1r_6_nibout));
  bshifter1r bshifter1r_7 (
    .sel(muxin), .shiftin({asix, arithin[31:28]}), .nibble(arithin[27:24]), .nibout(bshifter1r_7_nibout));
  bshifter1r bshifter1r_8 (.sel(muxin), .shiftin(aseven), .nibble(arithin[31:28]), .nibout(bshifter1r_8_nibout));

  // Other names for the same wires on the sheet: zerofi[23:0] = afive; zerof[19:0] = afour;
  //   aone[23:0] = arithin[31:8]; azero[27:0] = arithin[31:4]; testerin[31:0] = arithin; two[3:0] = arithin[11:8];
  //   zeroo[7:0] = aone; afive[7:0] = arithin[31:24]; afour[11:0] = arithin[31:20]; asix[3:0] = arithin[31:28];
  //   athree[15:0] = arithin[31:16]; atwo[19:0] = arithin[31:12]; seven[3:0] = arithin[31:28]; sbit = arithin[31];
  //   zerosi[27:0] = asix; zerothr[15:0] = athree; three[3:0] = arithin[15:12]; four[3:0] = arithin[19:16];
  //   five[3:0] = arithin[23:20]; six[3:0] = arithin[27:24]; zerotw[11:0] = atwo; one[3:0] = arithin[7:4];
  //   maybe[4:0] = bin[4:0]; outt[31:0] = outp; zero[3:0] = arithin[3:0]
endmodule

module bshifter1r (
  input  [4:0] sel,
  input  [31:0] shiftin,
  input  [3:0] nibble,
  output [3:0] nibout
);

  // Probe on {shiftin[27:0], nibble}
  bshift3r bshift3r_1 (.bin({shiftin[30:0], nibble[3]}), .muxval(sel), .bitout(nibout[3]));
  bshift3r bshift3r_2 (.bin({shiftin[29:0], nibble[3:2]}), .muxval(sel), .bitout(nibout[2]));
  bshift3r bshift3r_3 (.bin({shiftin[28:0], nibble[3:1]}), .muxval(sel), .bitout(nibout[1]));
  bshift3r bshift3r_4 (.bin({shiftin[27:0], nibble}), .muxval(sel), .bitout(nibout[0]));

  // Other names for the same wires on the sheet: a1[31:0] = {shiftin[27:0], nibble};
  //   a2[31:0] = {shiftin[28:0], nibble[3:1]}; a3[31:0] = {shiftin[29:0], nibble[3:2]};
  //   a4[31:0] = {shiftin[30:0], nibble[3]}; shifts[31:0] = shiftin; muxa[4:0] = sel
endmodule

module bshift3r (
  input  [31:0] bin,
  input  [4:0] muxval,
  output bitout
);

  Multiplexer #(.select(5), .enable("false")) multiplexer_1 (
    .in0(bin[0]), .in1(bin[1]), .in2(bin[2]), .in3(bin[3]), .in4(bin[4]), .in5(bin[5]), .in6(bin[6]),
    .in7(bin[7]), .in8(bin[8]), .in9(bin[9]), .in10(bin[10]), .in11(bin[11]), .in12(bin[12]), .in13(bin[13]),
    .in14(bin[14]), .in15(bin[15]), .in16(bin[16]), .in17(bin[17]), .in18(bin[18]), .in19(bin[19]),
    .in20(bin[20]), .in21(bin[21]), .in22(bin[22]), .in23(bin[23]), .in24(bin[24]), .in25(bin[25]),
    .in26(bin[26]), .in27(bin[27]), .in28(bin[28]), .in29(bin[29]), .in30(bin[30]), .in31(bin[31]),
    .out(bitout), .sel(muxval));
endmodule

module addertest (
  input  carryin,
  input  [31:0] ain,
  input  [31:0] bin,
  output co,
  output [31:0] sumout
);

  wire helper_adder_1_carryout, helper_adder_2_carryout, helper_adder_3_carryout, helper_adder_5_carryout,
       helper_adder_6_carryout, helper_adder_7_carryout, helper_adder_8_carryout;
  wire [3:0] xor_1_out, xor_2_out, xor_3_out, xor_4_out, xor_5_out, xor_6_out, xor_7_out, xor_8_out;

  assign xor_1_out = bin[3:0] ^ {4{carryin}};  // XOR_Gate xor_1, 4 bits wide
  helper_adder helper_adder_1 (
    .carryin(carryin), .ain(ain[3:0]), .bin(xor_1_out), .sum(sumout[3:0]), .carryout(helper_adder_1_carryout));
  assign xor_2_out = bin[11:8] ^ {4{carryin}};  // XOR_Gate xor_2, 4 bits wide
  assign xor_3_out = bin[7:4] ^ {4{carryin}};  // XOR_Gate xor_3, 4 bits wide
  assign xor_4_out = bin[31:28] ^ {4{carryin}};  // XOR_Gate xor_4, 4 bits wide
  helper_adder helper_adder_2 (
    .carryin(helper_adder_1_carryout), .ain(ain[7:4]), .bin(xor_3_out), .sum(sumout[7:4]),
    .carryout(helper_adder_2_carryout));
  helper_adder helper_adder_3 (
    .carryin(helper_adder_2_carryout), .ain(ain[11:8]), .bin(xor_2_out), .sum(sumout[11:8]),
    .carryout(helper_adder_3_carryout));
  assign xor_5_out = bin[15:12] ^ {4{carryin}};  // XOR_Gate xor_5, 4 bits wide
  helper_adder helper_adder_4 (
    .carryin(helper_adder_6_carryout), .ain(ain[31:28]), .bin(xor_4_out), .sum(sumout[31:28]), .carryout(co));
  assign xor_6_out = bin[27:24] ^ {4{carryin}};  // XOR_Gate xor_6, 4 bits wide
  assign xor_7_out = bin[19:16] ^ {4{carryin}};  // XOR_Gate xor_7, 4 bits wide
  helper_adder helper_adder_5 (
    .carryin(helper_adder_3_carryout), .ain(ain[15:12]), .bin(xor_5_out), .sum(sumout[15:12]),
    .carryout(helper_adder_5_carryout));
  assign xor_8_out = bin[23:20] ^ {4{carryin}};  // XOR_Gate xor_8, 4 bits wide
  helper_adder helper_adder_6 (
    .carryin(helper_adder_8_carryout), .ain(ain[27:24]), .bin(xor_6_out), .sum(sumout[27:24]),
    .carryout(helper_adder_6_carryout));
  helper_adder helper_adder_7 (
    .carryin(helper_adder_5_carryout), .ain(ain[19:16]), .bin(xor_7_out), .sum(sumout[19:16]),
    .carryout(helper_adder_7_carryout));
  helper_adder helper_adder_8 (
    .carryin(helper_adder_7_carryout), .ain(ain[23:20]), .bin(xor_8_out), .sum(sumout[23:20]),
    .carryout(helper_adder_8_carryout));

  // Other names for the same wires on the sheet: a1[3:0] = ain[3:0]; atest[31:0] = ain; a2[3:0] = ain[7:4];
  //   a3[3:0] = ain[11:8]; a4[3:0] = ain[15:12]; a5[3:0] = ain[19:16]; a6[3:0] = ain[23:20]; a7[3:0] = ain[27:24];
  //   a8[3:0] = ain[31:28]; b1[3:0] = bin[3:0]; btest[31:0] = bin; b2[3:0] = bin[7:4]; b3[3:0] = bin[11:8];
  //   b4[3:0] = bin[15:12]; b5[3:0] = bin[19:16]; b6[3:0] = bin[23:20]; b7[3:0] = bin[27:24]; b8[3:0] = bin[31:28];
  //   s1[3:0] = sumout[3:0]; s2[3:0] = sumout[7:4]; s3[3:0] = sumout[11:8]; s4[3:0] = sumout[15:12];
  //   s5[3:0] = sumout[19:16]; s6[3:0] = sumout[23:20]; s7[3:0] = sumout[27:24]; s8[3:0] = sumout[31:28];
  //   tc[3:0] = {4{carryin}}
endmodule

module slt4bit (
  input  [31:0] ain,
  input  [31:0] bin,
  output [31:0] sltout
);

  wire [31:0] subout;

  // Probe on ain
  // Probe on bin
  sub32 sub32_1 (.ain(ain), .bin(bin), .subout(subout));  // open: carin, cout
  // Probe on subout
  and and_1 (sltout[0], subout[31], 1'b1);

  assign sltout[31:1] = {31{1'b0}};

  // Other names for the same wires on the sheet: truthbit = sltout[0]
endmodule

module sub32 (
  input  [31:0] ain,
  input  carin,
  input  [31:0] bin,
  output cout,
  output [31:0] subout
);

  wire cot;
  wire [31:0] addertest_1_sumout, comp32_1_negout;

  // Probe on bin
  // Probe on comp32_1_negout
  comp32 comp32_1 (.a1(bin), .negout(comp32_1_negout));
  // Probe on ain
  addertest addertest_1 (.carryin(carin), .ain(comp32_1_negout), .bin(32'h1), .co(cot), .sumout(addertest_1_sumout));
  // Probe on addertest_1_sumout
  addertest addertest_2 (.carryin(cot), .ain(ain), .bin(addertest_1_sumout), .co(cout), .sumout(subout));
  // Probe on subout
  // Probe on subout

  // Other names for the same wires on the sheet: cotun = carin
endmodule

module subtest1 (
  input  in_1,
  input  [31:0] in_2,
  input  [31:0] in_3,
  output [31:0] out_4
);

  wire [31:0] comp32_1_negout;

  // Probe on comp32_1_negout
  comp32 comp32_1 (.a1(in_3), .negout(comp32_1_negout));
  addertest addertest_1 (.carryin(in_1), .ain(in_2), .bin(comp32_1_negout), .sumout(out_4));  // open: co
  // Probe on out_4
endmodule

module testbshifter1 (
  input  [4:0] shiftin,
  input  [31:0] ain,
  input  [3:0] nibin,
  output [3:0] nibout
);

  // Probe on ain[31:4]
  // Probe on {nibin, ain[31:4]}
  bshift3 bshift3_1 (.shifter({nibin, ain[31:4]}), .muxcon(shiftin), .bitout(nibout[3]));
  bshift3 bshift3_2 (.shifter({nibin[2:0], ain[31:3]}), .muxcon(shiftin), .bitout(nibout[2]));
  bshift3 bshift3_3 (.shifter({nibin[1:0], ain[31:2]}), .muxcon(shiftin), .bitout(nibout[1]));
  bshift3 bshift3_4 (.shifter({nibin[0], ain[31:1]}), .muxcon(shiftin), .bitout(nibout[0]));

  // Other names for the same wires on the sheet: a1[31:0] = {nibin[0], ain[31:1]}; shifts[31:0] = ain;
  //   a2[31:0] = {nibin[1:0], ain[31:2]}; a3[31:0] = {nibin[2:0], ain[31:3]}; a4[31:0] = {nibin, ain[31:4]};
  //   muxa[4:0] = shiftin
endmodule

module testshiftarith (
  input  [31:0] in_1,
  input  [31:0] in_2,
  output [31:0] out_3
);

  // Probe on in_1
  // Probe on in_2
  shiftrarith shiftrarith_1 (.arithin(in_1), .bin(in_2), .outp(out_3));
  // Probe on out_3
endmodule
