// Logisim project branch_comp.circ as structural Verilog: 4 circuits, main circuit branch_comp
module branch_comp (
  input  [31:0] rs1,
  input  [31:0] rs2,
  input  BrUn,
  output BrEq,
  output BrLt
);

  wire checkzero32bit_1_is_zero;
  wire [31:0] subout;

  // Probe on rs1
  // Probe on rs2
  sub32 sub32_1 (.ain(rs1), .bin(rs2), .subout(subout));  // open: carin, cout
  checkzero32bit checkzero32bit_1 (.zin(subout), .is_zero(checkzero32bit_1_is_zero));
  Multiplexer #(.enable("false")) multiplexer_1 (.in0(checkzero32bit_1_is_zero), .in1(1'b0), .out(BrEq), .sel(BrUn));
  Multiplexer #(.enable("false")) multiplexer_2 (.in0(subout[31]), .out(BrLt), .sel(BrUn));  // open: in1

  // Notes on the sheet:
  //   INPUTS to your circuit
  //   DON'T CHANGE THE LOCATIONS OF THE INPUTS AND OUTPUTS!
  //   OUTPUT from your circuit
endmodule

module checkzero4bit (
  input  [3:0] nib,
  output bout
);

  wire and_1_out, and_2_out, and_3_out, and_4_out;

  and and_1 (and_1_out, nib[0], 1'b1);
  and and_2 (and_2_out, nib[1], 1'b1);
  and and_3 (and_3_out, nib[2], 1'b1);
  and and_4 (and_4_out, nib[3], 1'b1);
  or or_1 (bout, and_1_out, and_2_out, and_3_out, and_4_out);
endmodule

module checkzero32bit (
  input  [31:0] zin,
  output is_zero
);

  wire n1, n2, n3, n4, n5, n6, n7, n8, or_1_out;

  checkzero4bit checkzero4bit_1 (.nib(zin[3:0]), .bout(n1));
  checkzero4bit checkzero4bit_2 (.nib(zin[7:4]), .bout(n2));
  checkzero4bit checkzero4bit_3 (.nib(zin[11:8]), .bout(n3));
  checkzero4bit checkzero4bit_4 (.nib(zin[15:12]), .bout(n4));
  checkzero4bit checkzero4bit_5 (.nib(zin[19:16]), .bout(n5));
  checkzero4bit checkzero4bit_6 (.nib(zin[23:20]), .bout(n6));
  checkzero4bit checkzero4bit_7 (.nib(zin[27:24]), .bout(n7));
  checkzero4bit checkzero4bit_8 (.nib(zin[31:28]), .bout(n8));
  or or_1 (or_1_out, n1, n2, n3, n4, n5, n6, n7, n8);
  not not_1 (is_zero, or_1_out);
endmodule

module test (
  input  [31:0] in_1
);

  wire checkzero4bit_1_p2, checkzero4bit_2_p2, checkzero4bit_3_p3, checkzero4bit_4_p3, checkzero4bit_5_p3,
       or_1_out;

  or or_1 (or_1_out, checkzero4bit_1_p2, checkzero4bit_2_p2, checkzero4bit_3_p3, checkzero4bit_4_p3);
  // checkzero4bit checkzero4bit_1: pin names not known; wires that end beside it: in_1[3:0], checkzero4bit_1_p2
  // checkzero4bit checkzero4bit_2: pin names not known; wires that end beside it: in_1[7:4], checkzero4bit_2_p2
  // checkzero4bit checkzero4bit_3: pin names not known; wires that end beside it: in_1[7:4], in_1[11:8], checkzero4bit_3_p3
  // checkzero4bit checkzero4bit_4: pin names not known; wires that end beside it: in_1[19:16], in_1[15:12], checkzero4bit_4_p3
  // checkzero4bit checkzero4bit_5: pin names not known; wires that end beside it: in_1[31:28], in_1[19:16], checkzero4bit_5_p3
  // checkzero4bit checkzero4bit_6: pin names not known; wires that end beside it: in_1[23:20]
  checkzero4bit checkzero4bit_7 (.nib(in_1[31:28]), .bout(in_1[24]));
  // checkzero4bit checkzero4bit_8: pin names not known; wires that end beside it: in_1[31:28]
  // Pins of 1 and 4 bits meet at in_1[27:24]
endmodule
