// Logisim project control_logic.circ as structural Verilog: 9 circuits, main circuit control_logic
module control_logic (
  input  [31:0] inst,
  input  BrEq,
  input  BrLt,
  output PCSel,
  output RegWEn,
  output [2:0] ImmSel,
  output BrUn,
  output ASel,
  output BSel,
  output [3:0] ALUSel,
  output MemRW,
  output [1:0] WBSel
);

  wire and_1_out, and_2_out, and_4_out, and_5_out, b0, b1, b2, i, is4, lt67, multiplexer_1_out, not_1_out,
       not_2_out, not_3_out, not_4_out, not_5_out, not_6_out, not_7_out, or_1_out, r, s, sb, uj;
  wire [1:0] wbsel_itype_1_wb_out;
  wire [3:0] asel_altrtype_1_sel_out, asel_itype_1_asel_out;
  wire [4:0] rd, rs1, rs2;
  wire [6:0] op;

  assign ALUSel = s ? 4'b0000 : 4'bz;  // Controlled_Buffer controlled_buffer_1
  // Probe on wbsel_itype_1_wb_out
  r_instructlogic r_instructlogic_1 (
    .in0(inst[2]), .in1(inst[3]), .in2(inst[4]), .in3(inst[5]), .in4(inst[6]), .tbit(r));
  s_instructlogic s_instructlogic_1 (
    .o0(inst[2]), .o1(inst[3]), .o2(inst[4]), .o3(inst[5]), .o4(inst[6]), .truthbit(s));
  assign ALUSel = sb ? 4'b0000 : 4'bz;  // Controlled_Buffer controlled_buffer_2
  assign RegWEn = sb ? 1'b0 : 1'bz;  // Controlled_Buffer controlled_buffer_3
  i_instructlogic i_instructlogic_1 (
    .op0(inst[2]), .op1(inst[3]), .op2(inst[4]), .op3(inst[5]), .op4(inst[6]), .iout(i));
  wbsel_itype wbsel_itype_1 (.op(op), .wb_out(wbsel_itype_1_wb_out));
  assign WBSel = i ? wbsel_itype_1_wb_out : 2'bz;  // Controlled_Buffer controlled_buffer_4
  // Probe on inst[31:25]
  sb_instructlogic sb_instructlogic_1 (
    .in0(inst[2]), .in1(inst[3]), .in2(inst[4]), .in3(inst[5]), .in4(inst[6]), .truthbit(sb));
  assign op = i ? inst[6:0] : 7'bz;  // Controlled_Buffer controlled_buffer_5
  assign rd = i ? inst[11:7] : 5'bz;  // Controlled_Buffer controlled_buffer_6
  assign {b2, b1, b0} = i ? inst[14:12] : 3'bz;  // Controlled_Buffer controlled_buffer_7
  assign rs1 = i ? inst[19:15] : 5'bz;  // Controlled_Buffer controlled_buffer_8
  assign ImmSel = i ? 3'b000 : 3'bz;  // Controlled_Buffer controlled_buffer_9
  assign ASel = i ? 1'b0 : 1'bz;  // Controlled_Buffer controlled_buffer_10
  assign BSel = i ? 1'b1 : 1'bz;  // Controlled_Buffer controlled_buffer_11
  // Probe on {b2, b1, b0}
  assign op = r ? inst[6:0] : 7'bz;  // Controlled_Buffer controlled_buffer_12
  assign rd = r ? inst[11:7] : 5'bz;  // Controlled_Buffer controlled_buffer_13
  assign {b2, b1, b0} = r ? inst[14:12] : 3'bz;  // Controlled_Buffer controlled_buffer_14
  assign rs1 = r ? inst[19:15] : 5'bz;  // Controlled_Buffer controlled_buffer_15
  assign rs2 = r ? inst[24:20] : 5'bz;  // Controlled_Buffer controlled_buffer_16
  Controlled_Buffer #(.width(3)) controlled_buffer_17 (.en(r));  // open: in, out
  assign ASel = r ? 1'b0 : 1'bz;  // Controlled_Buffer controlled_buffer_18
  assign BSel = r ? 1'b0 : 1'bz;  // Controlled_Buffer controlled_buffer_19
  assign op = s ? inst[6:0] : 7'bz;  // Controlled_Buffer controlled_buffer_20
  assign {b2, b1, b0} = s ? inst[14:12] : 3'bz;  // Controlled_Buffer controlled_buffer_21
  assign rs1 = s ? inst[19:15] : 5'bz;  // Controlled_Buffer controlled_buffer_22
  assign rs2 = s ? inst[24:20] : 5'bz;  // Controlled_Buffer controlled_buffer_23
  assign ImmSel = s ? 3'b010 : 3'bz;  // Controlled_Buffer controlled_buffer_24
  assign op = sb ? inst[6:0] : 7'bz;  // Controlled_Buffer controlled_buffer_25
  assign {b2, b1, b0} = sb ? inst[14:12] : 3'bz;  // Controlled_Buffer controlled_buffer_26
  assign rs1 = sb ? inst[19:15] : 5'bz;  // Controlled_Buffer controlled_buffer_27
  assign rs2 = sb ? inst[24:20] : 5'bz;  // Controlled_Buffer controlled_buffer_28
  // Probe on multiplexer_1_out
  assign RegWEn = i ? 1'b1 : 1'bz;  // Controlled_Buffer controlled_buffer_29
  assign PCSel = r ? 1'b0 : 1'bz;  // Controlled_Buffer controlled_buffer_30
  assign RegWEn = r ? 1'b1 : 1'bz;  // Controlled_Buffer controlled_buffer_31
  assign WBSel = r ? 2'b01 : 2'bz;  // Controlled_Buffer controlled_buffer_32
  assign ASel = s ? 1'b0 : 1'bz;  // Controlled_Buffer controlled_buffer_33
  assign BSel = s ? 1'b1 : 1'bz;  // Controlled_Buffer controlled_buffer_34
  assign PCSel = s ? 1'b0 : 1'bz;  // Controlled_Buffer controlled_buffer_35
  assign RegWEn = s ? 1'b0 : 1'bz;  // Controlled_Buffer controlled_buffer_36
  assign ImmSel = sb ? 3'b011 : 3'bz;  // Controlled_Buffer controlled_buffer_37
  Multiplexer #(.enable("false")) multiplexer_1 (.in0(1'b0), .in1(1'b1), .out(multiplexer_1_out), .sel(lt67));
  assign PCSel = i ? multiplexer_1_out : 1'bz;  // Controlled_Buffer controlled_buffer_38
  assign ASel = sb ? 1'b1 : 1'bz;  // Controlled_Buffer controlled_buffer_39
  assign BSel = sb ? 1'b1 : 1'bz;  // Controlled_Buffer controlled_buffer_40
  // Probe on {b2, b1, b0}
  and and_1 (and_1_out, BrLt, is4);
  and and_2 (and_2_out, BrEq, not_1_out);
  not not_1 (not_1_out, is4);
  assign MemRW = not_2_out ? 1'b0 : 1'bz;  // Controlled_Buffer controlled_buffer_41
  not not_2 (not_2_out, s);
  assign ImmSel = uj ? 3'b100 : 3'bz;  // Controlled_Buffer controlled_buffer_42
  not not_3 (not_3_out, b0);
  not not_4 (not_4_out, b1);
  or or_1 (or_1_out, and_1_out, and_2_out);
  and and_3 (is4, not_3_out, not_4_out, b2);
  assign PCSel = and_4_out ? 1'b1 : 1'bz;  // Controlled_Buffer controlled_buffer_43
  and and_4 (and_4_out, or_1_out, sb);
  not not_5 (not_5_out, op[3]);
  not not_6 (not_6_out, op[4]);
  assign MemRW = s ? 1'b1 : 1'bz;  // Controlled_Buffer controlled_buffer_44
  asel_itype asel_itype_1 (.f3_in({b2, b1, b0}), .asel_out(asel_itype_1_asel_out));
  asel_altrtype asel_altrtype_1 (.f3({b2, b1, b0}), .f7(inst[31:25]), .sel_out(asel_altrtype_1_sel_out));
  // Probe on asel_altrtype_1_sel_out
  uj_instructlogic uj_instructlogic_1 (
    .o0(inst[2]), .o1(inst[3]), .o2(inst[4]), .o3(inst[5]), .o4(inst[6]), .truthbit(uj));
  assign RegWEn = uj ? 1'b1 : 1'bz;  // Controlled_Buffer controlled_buffer_45
  assign WBSel = uj ? 2'b00 : 2'bz;  // Controlled_Buffer controlled_buffer_46
  assign ALUSel = i ? asel_itype_1_asel_out : 4'bz;  // Controlled_Buffer controlled_buffer_47
  assign ALUSel = r ? asel_altrtype_1_sel_out : 4'bz;  // Controlled_Buffer controlled_buffer_48
  assign op = uj ? inst[6:0] : 7'bz;  // Controlled_Buffer controlled_buffer_49
  assign rd = uj ? inst[11:7] : 5'bz;  // Controlled_Buffer controlled_buffer_50
  assign PCSel = and_5_out ? 1'b0 : 1'bz;  // Controlled_Buffer controlled_buffer_51
  and and_5 (and_5_out, not_7_out, sb);
  not not_7 (not_7_out, or_1_out);
  and and_6 (lt67, op[0], op[1], op[2], not_5_out, not_6_out, op[5], op[6]);
  assign ASel = uj ? 1'b1 : 1'bz;  // Controlled_Buffer controlled_buffer_52
  assign BSel = uj ? 1'b1 : 1'bz;  // Controlled_Buffer controlled_buffer_53
  assign ALUSel = uj ? 4'b0000 : 4'bz;  // Controlled_Buffer controlled_buffer_54
  assign PCSel = uj ? 1'b1 : 1'bz;  // Controlled_Buffer controlled_buffer_55

  assign BrUn = 1'b0;

  // Other names for the same wires on the sheet: funct3[2:0] = {b2, b1, b0}; op0 = inst[2]; op1 = inst[3];
  //   op2 = inst[4]; op3 = inst[5]; op4 = inst[6]; funct7[6:0] = inst[31:25]; r0 = op[0]; r1 = op[1]; r2 = op[2];
  //   r3 = op[3]; r4 = op[4]; r5 = op[5]; r6 = op[6]

  // Notes on the sheet:
  //   INPUTS to your circuit
  //   DON'T CHANGE THE LOCATIONS OF THE INPUTS AND OUTPUTS!
  //   OUTPUT from your circuit
endmodule

module i_instructlogic (
  input  op0,
  input  op1,
  input  op2,
  input  op3,
  input  op4,
  output iout
);

  wire and_1_out, and_2_out, and_3_out, not_1_out, not_2_out, not_3_out, not_4_out, not_5_out, not_6_out,
       not_7_out, not_8_out, not_9_out, not_10_out, not_11_out;

  not not_1 (not_1_out, op1);
  not not_2 (not_2_out, op2);
  not not_3 (not_3_out, op0);
  not not_4 (not_4_out, op1);
  not not_5 (not_5_out, op2);
  not not_6 (not_6_out, op3);
  not not_7 (not_7_out, op4);
  not not_8 (not_8_out, op0);
  not not_9 (not_9_out, op1);
  not not_10 (not_10_out, op3);
  not not_11 (not_11_out, op4);
  and and_1 (and_1_out, not_3_out, not_4_out, not_5_out, not_6_out, not_7_out);
  and and_2 (and_2_out, not_8_out, not_9_out, op2, not_10_out, not_11_out);
  and and_3 (and_3_out, op0, not_1_out, not_2_out, op3, op4);
  or or_1 (iout, and_3_out, and_1_out, and_2_out);
endmodule

module r_instructlogic (
  input  in0,
  input  in1,
  input  in2,
  input  in3,
  input  in4,
  output tbit
);

  wire not_1_out, not_2_out, not_3_out;

  not not_1 (not_1_out, in0);
  not not_2 (not_2_out, in1);
  not not_3 (not_3_out, in4);
  and and_1 (tbit, not_1_out, not_2_out, in2, in3, not_3_out);
endmodule

module s_instructlogic (
  input  o0,
  input  o1,
  input  o2,
  input  o3,
  input  o4,
  output truthbit
);

  wire not_1_out, not_2_out, not_3_out, not_4_out;

  not not_1 (not_1_out, o0);
  not not_2 (not_2_out, o1);
  not not_3 (not_3_out, o2);
  not not_4 (not_4_out, o4);
  and and_1 (truthbit, not_1_out, not_2_out, not_3_out, o3, not_4_out);
endmodule

module sb_instructlogic (
  input  in0,
  input  in1,
  input  in2,
  input  in3,
  input  in4,
  output truthbit
);

  wire not_1_out, not_2_out, not_3_out;

  not not_1 (not_1_out, in0);
  not not_2 (not_2_out, in1);
  not not_3 (not_3_out, in2);
  and and_1 (truthbit, not_1_out, not_2_out, not_3_out, in3, in4);
endmodule

module uj_instructlogic (
  input  o0,
  input  o1,
  input  o2,
  input  o3,
  input  o4,
  output truthbit
);

  wire not_1_out;

  not not_1 (not_1_out, o2);
  and and_1 (truthbit, o0, o1, not_1_out, o3, o4);
endmodule

module asel_itype (
  input  [2:0] f3_in,
  output [3:0] asel_out
);

  Multiplexer #(.select(3), .width(4), .enable("false")) multiplexer_1 (
    .in0(4'b0000), .in2(4'b0000), .in4(4'b0011), .in6(4'b0010), .in7(4'b0001), .out(asel_out), .sel(f3_in));  // open: in1, in3, in5

  // Other names for the same wires on the sheet: f3tun[2:0] = f3_in
endmodule

module wbsel_itype (
  input  [6:0] op,
  output [1:0] wb_out
);

  wire and_4_out, is_03, is_13, is_67, not_1_out, not_2_out, not_3_out, not_4_out, not_5_out, not_6_out,
       not_7_out, not_8_out, not_9_out, not_10_out, not_11_out, not_12_out, not_13_out, not_14_out;

  not not_1 (not_1_out, op[2]);
  not not_2 (not_2_out, op[3]);
  not not_3 (not_3_out, op[5]);
  not not_4 (not_4_out, op[6]);
  not not_5 (not_5_out, op[3]);
  not not_6 (not_6_out, op[4]);
  not not_7 (not_7_out, op[2]);
  not not_8 (not_8_out, op[3]);
  not not_9 (not_9_out, op[4]);
  not not_10 (not_10_out, op[5]);
  not not_11 (not_11_out, op[6]);
  and and_1 (is_13, op[0], op[1], not_1_out, not_2_out, op[4], not_3_out, not_4_out);
  and and_2 (is_67, op[0], op[1], op[2], not_5_out, not_6_out, op[5], op[6]);
  and and_3 (is_03, op[0], op[1], not_7_out, not_8_out, not_9_out, not_10_out, not_11_out);
  assign wb_out = is_13 ? 2'b01 : 2'bz;  // Controlled_Buffer controlled_buffer_1
  assign wb_out = is_67 ? 2'b00 : 2'bz;  // Controlled_Buffer controlled_buffer_2
  assign wb_out = is_03 ? 2'b10 : 2'bz;  // Controlled_Buffer controlled_buffer_3
  not not_12 (not_12_out, is_03);
  assign wb_out = and_4_out ? 2'b10 : 2'bz;  // Controlled_Buffer controlled_buffer_4
  and and_4 (and_4_out, not_12_out, not_13_out, not_14_out);
  not not_13 (not_13_out, is_13);
  not not_14 (not_14_out, is_67);

  // Other names for the same wires on the sheet: b0 = op[0]; b1 = op[1]; b2 = op[2]; b3 = op[3]; b4 = op[4];
  //   b5 = op[5]; b6 = op[6]; wt[1:0] = wb_out
endmodule

module asel_altrtype (
  input  [2:0] f3,
  input  [6:0] f7,
  output [3:0] sel_out
);

  wire and_7_out, and_8_out, and_9_out, and_10_out, and_11_out, not_1_out, not_2_out, not_3_out, not_4_out,
       not_5_out, not_6_out, not_7_out, not_8_out, not_9_out, not_10_out, not_11_out, not_12_out, not_13_out,
       not_14_out, t0, t1, t2, t5, t6, t7;

  not not_1 (not_1_out, f3[0]);
  not not_2 (not_2_out, f3[1]);
  not not_3 (not_3_out, f3[2]);
  not not_4 (not_4_out, f3[1]);
  not not_5 (not_5_out, f3[2]);
  not not_6 (not_6_out, f3[0]);
  not not_7 (not_7_out, f3[2]);
  not not_8 (not_8_out, f3[1]);
  not not_9 (not_9_out, f3[0]);
  and and_1 (t0, not_1_out, not_2_out, not_3_out);
  and and_2 (t1, f3[0], not_4_out, not_5_out);
  and and_3 (t2, not_6_out, f3[1], not_7_out);
  and and_4 (t5, f3[0], not_8_out, f3[2]);
  and and_5 (t6, not_9_out, f3[1], f3[2]);
  and and_6 (t7, f3[0], f3[1], f3[2]);
  and and_7 (and_7_out, t1, f7[0]);
  assign sel_out = t2 ? 4'b1000 : 4'bz;  // Controlled_Buffer controlled_buffer_1
  assign sel_out = t5 ? 4'b0101 : 4'bz;  // Controlled_Buffer controlled_buffer_2
  assign sel_out = t6 ? 4'b0010 : 4'bz;  // Controlled_Buffer controlled_buffer_3
  assign sel_out = t7 ? 4'b0001 : 4'bz;  // Controlled_Buffer controlled_buffer_4
  assign sel_out = and_7_out ? 4'b1011 : 4'bz;  // Controlled_Buffer controlled_buffer_5
  assign sel_out = and_8_out ? 4'b0110 : 4'bz;  // Controlled_Buffer controlled_buffer_6
  and and_8 (and_8_out, t1, not_10_out);
  not not_10 (not_10_out, f7[0]);
  assign sel_out = and_9_out ? 4'b1010 : 4'bz;  // Controlled_Buffer controlled_buffer_7
  and and_9 (and_9_out, t0, f7[0], not_11_out);
  not not_11 (not_11_out, f7[5]);
  // Probe on sel_out
  and and_10 (and_10_out, t0, not_12_out, not_13_out);
  not not_12 (not_12_out, f7[0]);
  assign sel_out = and_10_out ? 4'b0000 : 4'bz;  // Controlled_Buffer controlled_buffer_8
  not not_13 (not_13_out, f7[5]);
  assign sel_out = and_11_out ? 4'b1001 : 4'bz;  // Controlled_Buffer controlled_buffer_9
  and and_11 (and_11_out, t0, not_14_out, f7[5]);
  not not_14 (not_14_out, f7[0]);

  // Other names for the same wires on the sheet: ao[3:0] = sel_out; b0 = f3[0]; f3tun[2:0] = f3; b1 = f3[1];
  //   b2 = f3[2]; f7tun[6:0] = f7; f31sel = f7[0]; diff_f1 = f7[5]
endmodule
