// Logisim project cpu.circ as structural Verilog: 1 circuit, main circuit main
module main (
  input  [31:0] INSTRUCTION,
  input  CLOCK,
  input  in_3,
  input  in_4,
  input  in_5,
  output [31:0] PROGRAM_COUNTER,
  output [31:0] ra,
  output [31:0] sp,
  output [31:0] t0,
  output [31:0] t1,
  output [31:0] t2,
  output [31:0] s0,
  output [31:0] s1,
  output [31:0] a0
);

  wire branch_comp_1_breq, branch_comp_1_brlt, control_logic_1_asel, control_logic_1_brun,
       control_logic_1_bsel, control_logic_1_memrw, psel, rw;
  wire [1:0] control_logic_1_wbsel;
  wire [2:0] ims;
  wire [3:0] control_logic_1_alusel;
  wire [31:0] diff_inst, DMEM_read_data, imm, INSTRUCTION2, multiplexer_2_out, multiplexer_3_out,
       multiplexer_4_out, multiplexer_5_out, next_inst, pc4, PROGRAM_COUNTER2, recalc, rs1o, rs2o;

  // Probe on INSTRUCTION2
  control_logic control_logic_1 (
    .BSel(control_logic_1_bsel), .ASel(control_logic_1_asel), .BrUn(control_logic_1_brun), .ImmSel(ims),
    .RegWEn(rw), .PCSel(psel), .BrLt(branch_comp_1_brlt), .BrEq(branch_comp_1_breq), .inst(INSTRUCTION2),
    .ALUSel(control_logic_1_alusel), .MemRW(control_logic_1_memrw), .WBSel(control_logic_1_wbsel));
  Multiplexer #(.width(32), .enable("false")) multiplexer_1 (.in0(pc4), .in1(diff_inst), .out(next_inst), .sel(psel));
  // Probe on INSTRUCTION2[19:15]
  // Probe on next_inst
  addertest addertest_1 (.ain(PROGRAM_COUNTER), .bin(32'h4), .sumout(pc4));  // open: carryin, co
  // imm_gen imm_gen_1: pin names not known; wires that end beside it: INSTRUCTION2, ims, imm
  // Probe on imm
  // Probe on INSTRUCTION2
  Multiplexer #(.width(32), .enable("false")) multiplexer_2 (
    .in0(INSTRUCTION), .in1(32'h13), .out(multiplexer_2_out), .sel(psel));
  regfile32bit_falling regfile32bit_falling_1 (
    .r(in_5), .clk(CLOCK), .we(1'b1), .win(next_inst), .wout(PROGRAM_COUNTER));
  // Probe on INSTRUCTION
  // Probe on multiplexer_2_out
  // Probe on PROGRAM_COUNTER
  // Probe on INSTRUCTION2[24:20]
  // Probe on multiplexer_5_out
  // Probe on ra
  // Probe on INSTRUCTION2[19:15]
  // Probe on INSTRUCTION2[11:7]
  // Probe on ims
  regfile32bit_falling regfile32bit_falling_2 (
    .r(in_3), .clk(CLOCK), .we(1'b1), .win(PROGRAM_COUNTER), .wout(PROGRAM_COUNTER2));
  regfile32bit_falling regfile32bit_falling_3 (
    .r(in_4), .clk(CLOCK), .we(1'b1), .win(multiplexer_2_out), .wout(INSTRUCTION2));
  // Probe on sp
  // Probe on PROGRAM_COUNTER2
  // Probe on INSTRUCTION2
  // Probe on rs1o
  // Probe on t0
  // Probe on rw
  // Probe on rs2o
  regfile_main RegFile (
    .rs2(INSTRUCTION2[24:20]), .rd(INSTRUCTION2[11:7]), .Read_Data_1(rs1o), .Read_Data_2(rs2o), .ra(ra),
    .sp(sp), .t0(t0), .t1(t1), .t2(t2), .s0(s0), .s1(s1), .a0(a0), .rs1(INSTRUCTION2[19:15]),
    .Write_Data(multiplexer_5_out), .RegWEn(rw), .clk(CLOCK));  // open: in_1, in_2, in_7, in_12, in_14, in_16, in_4, in_9, in_13, in_15
  branch_comp branch_comp_1 (
    .BrEq(branch_comp_1_breq), .rs1(rs1o), .rs2(rs2o), .BrLt(branch_comp_1_brlt), .BrUn(control_logic_1_brun));
  // Probe on t1
  // Probe on control_logic_1_asel
  Multiplexer #(.width(32), .enable("false")) multiplexer_3 (
    .in0(rs1o), .in1(PROGRAM_COUNTER2), .out(multiplexer_3_out), .sel(control_logic_1_asel));
  // Probe on t2
  // Probe on rs2o
  Multiplexer #(.width(32), .enable("false")) multiplexer_4 (
    .in0(rs2o), .in1(imm), .out(multiplexer_4_out), .sel(control_logic_1_bsel));
  // Probe on control_logic_1_bsel
  // Probe on s0
  // Probe on rs1o
  // Probe on control_logic_1_alusel
  // Probe on diff_inst
  alu Arithmetic_Logic_Unit (
    .ALUSel(control_logic_1_alusel), .Result(diff_inst), .A(multiplexer_3_out), .B(multiplexer_4_out));
  // Probe on rs2o
  // Probe on multiplexer_5_out
  // Probe on DMEM_read_data
  mem_main DMEM (
    .Address(diff_inst), .Write_Data(rs2o), .Write_En(control_logic_1_memrw), .Read_Data(DMEM_read_data),
    .clk(CLOCK));
  addertest addertest_2 (.ain(PROGRAM_COUNTER2), .bin(32'h4), .sumout(recalc));  // open: carryin, co
  // Probe on control_logic_1_wbsel
  Multiplexer #(.select(2), .width(32), .enable("false")) multiplexer_5 (
    .in0(recalc), .in1(diff_inst), .in2(DMEM_read_data), .out(multiplexer_5_out), .sel(control_logic_1_wbsel));  // open: in3

  // Other names for the same wires on the sheet: clk = CLOCK; rdb[4:0] = INSTRUCTION2[11:7];
  //   rs1b[4:0] = INSTRUCTION2[19:15]; rs2[4:0] = INSTRUCTION2[24:20]

  // Notes on the sheet:
  //   Output
  //   IMEM (do **NOT** move this)
  //   Inputs
  //   It is OK to move the PC, RegFile, ALU, MEM, Branch Comp, Imm Gen, and Control Logic to wherever is most convenient for you when constructing your CPU, and to delete this text
  //   Inputs/Outputs for testing. Do **NOT** move these.
endmodule
