// Logisim project imm_gen.circ as structural Verilog: 1 circuit, main circuit imm_gen
module imm_gen (
  input  [31:0] inst,
  input  [2:0] ImmSel,
  output [31:0] imm
);

  wire [31:0] iw1, iw3, iw4, iw5;

  Multiplexer #(.select(3), .width(32), .enable("false")) multiplexer_1 (
    .in0(iw1), .in1({32{1'b0}}), .in2(iw3), .in3(iw4), .in4(iw5), .out(imm), .sel(ImmSel));  // open: in5, in6, in7
  assign iw1 = {{20{inst[31]}}, inst[31:20]};  // Bit_Extender bit_extender_1
  assign iw3 = {{20{inst[31]}}, {inst[31:25], inst[11:7]}};  // Bit_Extender bit_extender_2
  assign iw4 = {{19{inst[31]}}, {inst[31], inst[7], inst[30:25], inst[11:8], 1'b0}};  // Bit_Extender bit_extender_3
  assign iw5 = {{11{inst[31]}}, {inst[31], inst[19:12], inst[20], inst[30:21], 1'b0}};  // Bit_Extender bit_extender_4

  // Other names for the same wires on the sheet: i3[11:0] = {inst[31:25], inst[11:7]};
  //   i4[12:1] = {inst[31], inst[7], inst[30:25], inst[11:8]}; i1[11:0] = inst[31:20];
  //   i5[20:1] = {inst[31], inst[19:12], inst[20], inst[30:21]}

  // Notes on the sheet:
  //   INPUTS to your circuit
  //   DON'T CHANGE THE LOCATIONS OF THE INPUTS AND OUTPUTS!
  //   OUTPUT from your circuit
endmodule
