// Logisim project mem.circ as structural Verilog: 2 circuits, main circuit main
module main (
  input  [31:0] Address,
  input  Write_En,
  input  clk,
  input  [31:0] Write_Data,
  output [31:0] Read_Data
);

  wire mem_latch_1_read_en, mem_latch_1_we_latched;
  wire [31:0] mem_latch_1_address_latched, mem_latch_1_data_in_latched;

  mem_latch mem_latch_1 (
    .address(Address), .we(Write_En), .clk(clk), .data_in(Write_Data),
    .address_latched(mem_latch_1_address_latched), .we_latched(mem_latch_1_we_latched),
    .read_en(mem_latch_1_read_en), .data_in_latched(mem_latch_1_data_in_latched));
  RAM #(.addrWidth(14), .dataWidth(32), .trigger("high"), .databus("bibus")) ram_1 (
    .addr(mem_latch_1_address_latched[15:2]), .we(mem_latch_1_we_latched), .oe(mem_latch_1_read_en),
    .din(mem_latch_1_data_in_latched), .dout(Read_Data));
endmodule

module mem_latch (
  input  [31:0] address,
  input  we,
  input  clk,
  input  [31:0] data_in,
  output [31:0] address_latched,
  output we_latched,
  output read_en,
  output [31:0] data_in_latched
);

  wire d_ff_1_q;
  wire [31:0] register_1_q;

  Register #(.width(32), .trigger("falling")) register_1 (
    .D(address), .en(we), .clk(clk), .Q(register_1_q));  // open: clr
  Register #(.width(32), .trigger("falling")) register_2 (
    .D(data_in), .en(we), .clk(clk), .Q(data_in_latched));  // open: clr
  D_Flip_Flop #(.trigger("falling")) d_ff_1 (.D(we), .clk(clk), .Q(d_ff_1_q));  // open: Qn, preset, reset
  Multiplexer #(.width(32), .enable("false")) multiplexer_1 (
    .in0(address), .in1(register_1_q), .out(address_latched), .sel(d_ff_1_q));
  and and_1 (we_latched, clk, d_ff_1_q);
  not not_1 (read_en, we_latched);
endmodule
