// Logisim project regfile.circ as structural Verilog: 9 circuits, main circuit main
module main (
  input  [31:0] in_1,
  input  in_2,
  input  [4:0] rs1,
  input  in_4,
  input  [4:0] rs2,
  input  [4:0] rd,
  input  in_7,
  input  [31:0] Write_Data,
  input  in_9,
  input  RegWEn,
  input  clk,
  input  in_12,
  input  in_13,
  input  in_14,
  input  in_15,
  input  in_16,
  output [31:0] ra,
  output [31:0] sp,
  output [31:0] t0,
  output [31:0] t1,
  output [31:0] t2,
  output [31:0] s0,
  output [31:0] s1,
  output [31:0] a0,
  output [31:0] Read_Data_1,
  output [31:0] Read_Data_2
);

  wire and_1_out, and_2_out, and_3_out, and_4_out, and_5_out, and_6_out, and_7_out, and_8_out, x0ow, x1ow,
       x2ow, x5ow, x6ow, x7ow, x8ow, x9ow, x10ow;

  Decoder #(.select(5), .enable("false")) decoder_1 (
    .out0(x0ow), .out1(x1ow), .out2(x2ow), .out5(x5ow), .out6(x6ow), .out7(x7ow), .out8(x8ow), .out9(x9ow),
    .out10(x10ow), .sel(rd));  // open: out3, out4, out11, out12, out13, out14, out15, out16, out17, out18, out19, out20, out21, out22, out23, out24, out25, out26, out27, out28, out29, out30, out31
  and and_1 (and_1_out, x1ow, RegWEn);
  and and_2 (and_2_out, x2ow, RegWEn);
  and and_3 (and_3_out, x5ow, RegWEn);
  and and_4 (and_4_out, x6ow, RegWEn);
  regfile32bit regfile32bit_1 (.reset(in_2), .clk(clk), .we(1'b0), .wordin({32{1'b0}}), .wordout(in_1));
  regfile32bit regfile32bit_2 (.reset(in_7), .clk(clk), .we(and_1_out), .wordin(Write_Data), .wordout(ra));
  regfile32bit regfile32bit_3 (.reset(in_12), .clk(clk), .we(and_2_out), .wordin(Write_Data), .wordout(sp));
  regfile32bit regfile32bit_4 (.reset(in_14), .clk(clk), .we(and_3_out), .wordin(Write_Data), .wordout(t0));
  regfile32bit regfile32bit_5 (.reset(in_16), .clk(clk), .we(and_4_out), .wordin(Write_Data), .wordout(t1));
  and and_5 (and_5_out, x7ow, RegWEn);
  and and_6 (and_6_out, x8ow, RegWEn);
  and and_7 (and_7_out, x9ow, RegWEn);
  and and_8 (and_8_out, x10ow, RegWEn);
  regfile32bit regfile32bit_6 (.reset(in_4), .clk(clk), .we(and_5_out), .wordin(Write_Data), .wordout(t2));
  regfile32bit regfile32bit_7 (.reset(in_9), .clk(clk), .we(and_6_out), .wordin(Write_Data), .wordout(s0));
  regfile32bit regfile32bit_8 (.reset(in_13), .clk(clk), .we(and_7_out), .wordin(Write_Data), .wordout(s1));
  regfile32bit regfile32bit_9 (.reset(in_15), .clk(clk), .we(and_8_out), .wordin(Write_Data), .wordout(a0));
  Multiplexer #(.select(5), .width(32), .enable("false")) multiplexer_1 (
    .in0(in_1), .in1(ra), .in2(sp), .in5(t0), .in6(t1), .in7(t2), .in8(s0), .in9(s1), .in10(a0),
    .out(Read_Data_1), .sel(rs1));  // open: in3, in4, in11, in12, in13, in14, in15, in16, in17, in18, in19, in20, in21, in22, in23, in24, in25, in26, in27, in28, in29, in30, in31
  Multiplexer #(.select(5), .width(32), .enable("false")) multiplexer_2 (
    .in0(in_1), .in1(ra), .in2(sp), .in5(t0), .in6(t1), .in7(t2), .in8(s0), .in9(s1), .in10(a0),
    .out(Read_Data_2), .sel(rs2));  // open: in3, in4, in11, in12, in13, in14, in15, in16, in17, in18, in19, in20, in21, in22, in23, in24, in25, in26, in27, in28, in29, in30, in31
  // Probe on rs2

  // Other names for the same wires on the sheet: a0a[31:0] = a0; raa[31:0] = ra; read_data1[31:0] = Read_Data_1;
  //   read_data2[31:0] = Read_Data_2; read_reg1[4:0] = rs1; read_reg2[4:0] = rs2; s0a[31:0] = s0; s1a[31:0] = s1;
  //   spa[31:0] = sp; t0a[31:0] = t0; t1a[31:0] = t1; t2a[31:0] = t2; write_en = RegWEn; write_reg[4:0] = rd;
  //   x0a[31:0] = in_1; z[31:0] = in_1

  // Notes on the sheet:
  //   INPUTS to your circuit
  //   DON'T CHANGE THE LOCATIONS OF THE INPUTS AND OUTPUTS!
  //   These are DEBUG/TEST outputs from your circuit.
  //   OUTPUTS from your circuit
endmodule

module regfile4bit (
  input  reset,
  input  [3:0] bitin,
  input  clk,
  input  we,
  output [3:0] nibout
);

  wire and_1_out, and_2_out, and_3_out, and_4_out;

  and and_1 (and_1_out, we, clk);
  and and_2 (and_2_out, we, clk);
  and and_3 (and_3_out, we, clk);
  D_Flip_Flop d_ff_1 (.D(bitin[0]), .clk(and_4_out), .Q(nibout[0]), .reset(reset));  // open: Qn, preset
  and and_4 (and_4_out, we, clk);
  D_Flip_Flop d_ff_2 (.D(bitin[1]), .clk(and_1_out), .Q(nibout[1]), .reset(reset));  // open: Qn, preset
  D_Flip_Flop d_ff_3 (.D(bitin[2]), .clk(and_2_out), .Q(nibout[2]), .reset(reset));  // open: Qn, preset
  D_Flip_Flop d_ff_4 (.D(bitin[3]), .clk(and_3_out), .Q(nibout[3]), .reset(reset));  // open: Qn, preset

  // Other names for the same wires on the sheet: c = clk; w = we
endmodule

module regfile16bit (
  input  clk16,
  input  r16,
  input  we,
  input  [15:0] hwin,
  output [15:0] hwout
);

  regfile4bit regfile4bit_1 (.reset(r16), .bitin(hwin[3:0]), .clk(clk16), .we(we), .nibout(hwout[3:0]));
  regfile4bit regfile4bit_2 (.reset(r16), .bitin(hwin[7:4]), .clk(clk16), .we(we), .nibout(hwout[7:4]));
  regfile4bit regfile4bit_3 (.reset(r16), .bitin(hwin[11:8]), .clk(clk16), .we(we), .nibout(hwout[11:8]));
  regfile4bit regfile4bit_4 (.reset(r16), .bitin(hwin[15:12]), .clk(clk16), .we(we), .nibout(hwout[15:12]));

  // Other names for the same wires on the sheet: clk1 = clk16; n0[3:0] = hwout[3:0]; n1[3:0] = hwout[7:4];
  //   n2[3:0] = hwout[11:8]; n3[3:0] = hwout[15:12]; r1 = r16
endmodule

module regfile32bit (
  input  reset,
  input  clk,
  input  we,
  input  [31:0] wordin,
  output [31:0] wordout
);

  regfile16bit regfile16bit_1 (.clk16(clk), .r16(reset), .we(we), .hwin(wordin[15:0]), .hwout(wordout[15:0]));
  regfile16bit regfile16bit_2 (.clk16(clk), .r16(reset), .we(we), .hwin(wordin[31:16]), .hwout(wordout[31:16]));

  // Other names for the same wires on the sheet: clkw = clk; rw = reset
endmodule

module regfile4bit_falling (
  input  reset,
  input  [3:0] nibin,
  input  clk,
  input  we,
  output [3:0] nibout
);

  wire and_1_out, and_2_out, and_3_out, and_4_out;

  and and_1 (and_1_out, we, clk);
  and and_2 (and_2_out, we, clk);
  and and_3 (and_3_out, we, clk);
  D_Flip_Flop #(.trigger("falling")) d_ff_1 (
    .D(nibin[0]), .clk(and_4_out), .Q(nibout[0]), .reset(reset));  // open: Qn, preset
  and and_4 (and_4_out, we, clk);
  D_Flip_Flop #(.trigger("falling")) d_ff_2 (
    .D(nibin[1]), .clk(and_1_out), .Q(nibout[1]), .reset(reset));  // open: Qn, preset
  D_Flip_Flop #(.trigger("falling")) d_ff_3 (
    .D(nibin[2]), .clk(and_2_out), .Q(nibout[2]), .reset(reset));  // open: Qn, preset
  D_Flip_Flop #(.trigger("falling")) d_ff_4 (
    .D(nibin[3]), .clk(and_3_out), .Q(nibout[3]), .reset(reset));  // open: Qn, preset

  // Other names for the same wires on the sheet: c = clk; w = we
endmodule

module regfile16bit_falling (
  input  clk,
  input  r,
  input  w,
  input  [15:0] nin,
  output [15:0] nout
);

  // Probe on nin[15:12]
  // Probe on nin[11:8]
  // Probe on nin[3:0]
  // Probe on nin[7:4]
  // Probe on nout[3:0]
  regfile4bit_falling regfile4bit_falling_1 (.reset(r), .nibin(nin[3:0]), .clk(clk), .we(w), .nibout(nout[3:0]));
  // Probe on nout[7:4]
  regfile4bit_falling regfile4bit_falling_2 (.reset(r), .nibin(nin[7:4]), .clk(clk), .we(w), .nibout(nout[7:4]));
  // Probe on nout[11:8]
  regfile4bit_falling regfile4bit_falling_3 (.reset(r), .nibin(nin[11:8]), .clk(clk), .we(w), .nibout(nout[11:8]));
  // Probe on nout[15:12]
  regfile4bit_falling regfile4bit_falling_4 (.reset(r), .nibin(nin[15:12]), .clk(clk), .we(w), .nibout(nout[15:12]));

  // Other names for the same wires on the sheet: clk1 = clk; n0[3:0] = nout[3:0]; n1[3:0] = nout[7:4];
  //   n2[3:0] = nout[11:8]; n3[3:0] = nout[15:12]; r1 = r; we = w
endmodule

module regfile32bit_falling (
  input  r,
  input  clk,
  input  we,
  input  [31:0] win,
  output [31:0] wout
);

  // Probe on win[15:0]
  // Probe on win[31:16]
  regfile16bit_falling regfile16bit_falling_1 (.clk(clk), .r(r), .w(we), .nin(win[15:0]), .nout(wout[15:0]));
  regfile16bit_falling regfile16bit_falling_2 (.clk(clk), .r(r), .w(we), .nin(win[31:16]), .nout(wout[31:16]));
  // Probe on wout[15:0]
  // Probe on wout[31:16]

  // Other names for the same wires on the sheet: clkw = clk; rw = r
endmodule

module regfile_alt (
  input  in_1,
  input  [3:0] ain,
  input  in_3,
  input  in_4,
  input  in_5,
  input  [3:0] in_6,
  input  in_7,
  input  in_8,
  output [3:0] out_9,
  output [3:0] out_10
);

  wire and_1_out, and_2_out, and_3_out, and_4_out, and_5_out, and_6_out, and_7_out, and_8_out;

  and and_1 (and_1_out, in_5, ~in_4);  // AND_Gate
  and and_2 (and_2_out, in_5, ~in_4);  // AND_Gate
  and and_3 (and_3_out, in_5, ~in_4);  // AND_Gate
  D_Flip_Flop d_ff_1 (.D(ain[0]), .clk(and_4_out), .Q(out_9[0]), .reset(in_1));  // open: Qn, preset
  and and_4 (and_4_out, in_5, ~in_4);  // AND_Gate
  D_Flip_Flop d_ff_2 (.D(ain[1]), .clk(and_1_out), .Q(out_9[1]), .reset(in_1));  // open: Qn, preset
  D_Flip_Flop d_ff_3 (.D(ain[2]), .clk(and_2_out), .Q(out_9[2]), .reset(in_1));  // open: Qn, preset
  D_Flip_Flop d_ff_4 (.D(ain[3]), .clk(and_3_out), .Q(out_9[3]), .reset(in_1));  // open: Qn, preset
  and and_5 (and_5_out, in_5, in_4);
  and and_6 (and_6_out, in_5, in_4);
  and and_7 (and_7_out, in_5, in_4);
  D_Flip_Flop d_ff_5 (.D(in_6[0]), .clk(and_8_out), .Q(out_10[0]), .reset(in_1));  // open: Qn, preset
  and and_8 (and_8_out, in_5, in_4);
  D_Flip_Flop d_ff_6 (.D(in_6[1]), .clk(and_5_out), .Q(out_10[1]), .reset(in_1));  // open: Qn, preset
  D_Flip_Flop d_ff_7 (.D(in_6[2]), .clk(and_6_out), .Q(out_10[2]), .reset(in_1));  // open: Qn, preset
  D_Flip_Flop d_ff_8 (.D(in_6[3]), .clk(and_7_out), .Q(out_10[3]), .reset(in_1));  // open: Qn, preset

  assign in_3 = in_1;
  assign in_7 = in_4;
  assign in_8 = in_5;

  // Other names for the same wires on the sheet: c = in_4; reset = in_1; w = in_5
endmodule

module regfile_16bitalt (
  input  in_1,
  input  in_2,
  input  in_3,
  output [15:0] out_4
);

  wire [3:0] undriven, undriven_2, undriven_3, undriven_4;

  // Probe on undriven_4
  // Probe on undriven_3
  // Probe on undriven
  // Probe on undriven_2
  // Probe on out_4[3:0]
  // Probe on out_4[7:4]
  // Probe on out_4[11:8]
  // Probe on out_4[15:12]

  // Other names for the same wires on the sheet: clk1 = in_1; n0[3:0] = out_4[3:0]; n1[3:0] = out_4[7:4];
  //   n2[3:0] = out_4[11:8]; n3[3:0] = out_4[15:12]; r1 = in_2; we = in_3
endmodule
