// Logisim project signedmultiplier.circ as structural Verilog: 1 circuit, main circuit main
module main (
  input  [31:0] A,
  input  [31:0] B,
  output [31:0] result,
  output [31:0] result_high
);

  wire and_1_out, nor_1_out, not_1_out, not_2_out, xor_1_out;
  wire [31:0] adder_1_out, controlled_buffer_2_out, multiplier_1_cout, subtractor_1_out, subtractor_2_out;

  Multiplier #(.width(32)) multiplier_1 (.a(A), .b(B), .out(result), .cout(multiplier_1_cout));  // open: cin
  nor nor_1 (nor_1_out, A[31], B[31]);
  assign result_high = nor_1_out ? multiplier_1_cout : 32'bz;  // Controlled_Buffer controlled_buffer_1
  not not_1 (not_1_out, A[31]);
  not not_2 (not_2_out, B[31]);
  assign controlled_buffer_2_out = not_1_out ? A : 32'bz;  // Controlled_Buffer controlled_buffer_2
  assign controlled_buffer_2_out = not_2_out ? B : 32'bz;  // Controlled_Buffer controlled_buffer_3
  xor xor_1 (xor_1_out, A[31], B[31]);
  Adder #(.width(32)) adder_1 (.a(A), .b(B), .out(adder_1_out));  // open: cin, cout
  assign result_high = xor_1_out ? subtractor_2_out : 32'bz;  // Controlled_Buffer controlled_buffer_4
  Subtractor #(.width(32)) subtractor_1 (
    .a(multiplier_1_cout), .b(adder_1_out), .out(subtractor_1_out));  // open: bin, bout
  Subtractor #(.width(32)) subtractor_2 (
    .a(multiplier_1_cout), .b(controlled_buffer_2_out), .out(subtractor_2_out));  // open: bin, bout
  and and_1 (and_1_out, A[31], B[31]);
  assign result_high = and_1_out ? subtractor_1_out : 32'bz;  // Controlled_Buffer controlled_buffer_5

  // Notes on the sheet:
  //   Don't analyse this circuit.
  //   It's hacky. Besides, multiplication cannot be done in a single cycle, and even Logisim is faking it.
  //   - Anshu
endmodule
